# Fritzing sketch UV_Tester (saved by Fritzing 0.9.5d)

parts:
  부품1 = GUVA-S12SD UV Light Sensor
  부품2 = Arduino Nano (Rev3.0)
  S2 = Pushbutton [package="[SMD]"]
  LCD1 = LCD screen
  LCM1602_IIC1 = LCM1602 IIC [part_number="LCM1602 IIC" chip_label="LCM1602 IIC" package="DIP (Dual Inline) [THT]"]
  R1 = Resistor [tolerance=±5% resistance=10k package=THT]
  Power_plug1 = Power plug  # not connected

nets:
  5V: 부품1.5V, 부품2.3V3
  N1: 부품1.Out, 부품2.A1, 부품2.A0
  GND: 부품1.GND, 부품2.GND, LCM1602_IIC1.GND, R1.Pin_1
  N2: 부품2.D2, S2.Pin_3, S2.Pin_4, R1.Pin_0
  5V_2: 부품2.5V, S2.Pin_1, S2.Pin_2, LCM1602_IIC1.VCC
  N3: 부품2.A5, LCM1602_IIC1.SDA
  N4: 부품2.A4, LCM1602_IIC1.SCL
  VSS: LCD1.VSS, LCM1602_IIC1.VSS
  VDD: LCD1.VDD, LCM1602_IIC1.VDD
  N5: LCD1.V0, LCM1602_IIC1.V0
  N6: LCD1.RS, LCM1602_IIC1.RS
  N7: LCD1.R/W, LCM1602_IIC1.RW
  N8: LCD1.E, LCM1602_IIC1.E
  N9: LCD1.DB0, LCM1602_IIC1.D0
  N10: LCD1.DB1, LCM1602_IIC1.D1
  N11: LCD1.DB2, LCM1602_IIC1.D2
  N12: LCD1.DB3, LCM1602_IIC1.D3
  N13: LCD1.DB4, LCM1602_IIC1.D4
  N14: LCD1.DB5, LCM1602_IIC1.D5
  N15: LCD1.DB6, LCM1602_IIC1.D6
  N16: LCD1.DB7, LCM1602_IIC1.D7
  N17: LCD1.LED+, LCM1602_IIC1.A
  N18: LCD1.LED-, LCM1602_IIC1.K
  N19: LCM1602_IIC1.LED_A, LCM1602_IIC1.LED_B

custom parts:
  GUVA-S12SD UV Light Sensor: Extend your light-sensing spectrum with this analog UV sensor module. It uses a UV photodiode, which can detect the 240-370nm range of light (which covers UVB and most of UVA spectrum). The signal level from the photodiode is very small, in the nano-ampere level, so we tossed on an opamp to amplify the signal to a more manageable volt-level.
  LCM1602 IIC: I2C-Module to use a 1602 or 2004 LCD on with the wire.h libory Serial LCD Modul
